// Logisim project lab10.circ as structural Verilog: 4 circuits, main circuit main
module main (
  input  Reset_CPU,
  input  clock,
  output [7:0] Reg__A,
  output [7:0] B,
  output [7:0] PC,
  output [15:0] instruction
);

  wire control_unit_1_destmux, fields_1_register, not_1_out;
  wire [1:0] control_unit_1_aluop;
  wire [3:0] fields_1_op;
  wire [7:0] adder_1_out, alu_1_out, fields_1_immediate, multiplexer_1_out;

  Adder adder_1 (.a(PC), .b(8'h1), .out(adder_1_out));  // open: cin, cout
  Register u_PC (.D(adder_1_out), .en(1'b1), .Q(PC), .clk(clock), .clr(Reset_CPU));
  ROM #(.dataWidth(16)) rom_1 (.addr(PC), .data(instruction), .sel(1'b1));
  Fields fields_1 (.in_1(instruction), .Immediate(fields_1_immediate), .Register(fields_1_register), .Op(fields_1_op));
  Control_Unit control_unit_1 (.Opcode(fields_1_op), .ALUop(control_unit_1_aluop), .DestMux(control_unit_1_destmux));
  Multiplexer #(.width(8), .enable("false")) multiplexer_1 (
    .in0(alu_1_out), .in1(fields_1_immediate), .out(multiplexer_1_out), .sel(control_unit_1_destmux));
  not not_1 (not_1_out, fields_1_register);
  Register A (.D(multiplexer_1_out), .en(not_1_out), .Q(Reg__A), .clk(clock), .clr(Reset_CPU));
  Register u_B (.D(multiplexer_1_out), .en(fields_1_register), .Q(B), .clk(clock), .clr(Reset_CPU));
  ALU alu_1 (.ALU_OP(control_unit_1_aluop), .A(Reg__A), .B(B), .Out(alu_1_out));

  // Notes on the sheet:
  //   contents of rom_1 (hex, n*v repeats v):
  //   1 802 2800 1 5800
endmodule

// Flds
module Fields (
  input  [15:0] in_1,
  output [7:0] Immediate,
  output Register,
  output [3:0] Op
);


  assign Immediate = in_1[7:0];
  assign Op = in_1[15:12];
  assign Register = in_1[11];
endmodule

module ALU (
  input  [1:0] ALU_OP,
  input  [7:0] A,
  input  [7:0] B,
  output [7:0] Out
);

  wire [7:0] adder_1_out, and_1_out, or_1_out, subtractor_1_out;

  assign or_1_out = A | B;  // OR_Gate or_1, 8 bits wide
  assign and_1_out = A & B;  // AND_Gate and_1, 8 bits wide
  Adder adder_1 (.a(A), .b(B), .out(adder_1_out));  // open: cin, cout
  Subtractor subtractor_1 (.a(A), .b(B), .out(subtractor_1_out));  // open: bin, bout
  Multiplexer #(.select(2), .width(8), .enable("false")) multiplexer_1 (
    .in0(or_1_out), .in1(and_1_out), .in2(adder_1_out), .in3(subtractor_1_out), .out(Out), .sel(ALU_OP));
endmodule

// CU
module Control_Unit (
  input  [3:0] Opcode,
  output [1:0] ALUop,
  output DestMux
);

  wire or_1_out;

  not not_1 (DestMux, or_1_out);
  or or_1 (or_1_out, Opcode[0], Opcode[1], Opcode[2]);

  assign ALUop = Opcode[1:0];
endmodule
