// Logisim project lab08.circ as structural Verilog: 3 circuits, main circuit main
module main (
  input  [3:0] in_1,
  input  [7:0] in_2,
  input  [7:0] in_3,
  output out_4,
  output [7:0] out_5,
  output out_6
);

  _8BitALU u_8bitalu_1 (.Inputs(in_1), .in_2(in_2), .in_3(in_3), .Result(out_5), .Zero(out_4), .Overflow(out_6));

  // Notes on the sheet:
  //   0 = and
  //   1 = or
  //   2 = Addition
  //   3 = Less
endmodule

module _1bitALU (
  input  [1:0] OPPERATION,
  input  A_INVERT,
  input  in_3,
  input  CARRY_IN,
  input  A,
  input  B,
  input  LESS,
  output RESULT,
  output CARRYOUT,
  output SET
);

  wire and_1_out, multiplexer_1_out, multiplexer_2_out, not_1_out, not_2_out, or_1_out;

  not not_1 (not_1_out, A);
  not not_2 (not_2_out, B);
  Multiplexer multiplexer_1 (.in0(A), .in1(not_1_out), .out(multiplexer_1_out), .sel(A_INVERT));  // open: en
  Multiplexer multiplexer_2 (.in0(B), .in1(not_2_out), .out(multiplexer_2_out), .sel(in_3));  // open: en
  and and_1 (and_1_out, multiplexer_1_out, multiplexer_2_out);
  or or_1 (or_1_out, multiplexer_1_out, multiplexer_2_out);
  Adder #(.width(1)) adder_1 (.a(multiplexer_1_out), .b(multiplexer_2_out), .out(SET), .cin(CARRY_IN), .cout(CARRYOUT));
  Multiplexer #(.select(2)) multiplexer_3 (
    .in0(and_1_out), .in1(or_1_out), .in2(SET), .in3(LESS), .out(RESULT), .sel(OPPERATION));  // open: en

  // Notes on the sheet:
  //   BINVERT
endmodule

module _8BitALU (
  input  [3:0] Inputs,
  input  [7:0] in_2,
  input  [7:0] in_3,
  output [7:0] Result,
  output Zero,
  output Overflow
);

  wire n1bitalu_1_carryout, n1bitalu_2_carryout, n1bitalu_3_carryout, n1bitalu_4_carryout,
       n1bitalu_5_carryout, n1bitalu_6_carryout, n1bitalu_7_carryout, n1bitalu_8_set, or_1_out;

  _1bitALU u_1bitalu_1 (
    .A(in_2[0]), .B(in_3[0]), .LESS(n1bitalu_8_set), .A_INVERT(Inputs[3]), .in_3(Inputs[2]),
    .CARRY_IN(Inputs[2]), .OPPERATION(Inputs[1:0]), .CARRYOUT(n1bitalu_1_carryout), .RESULT(Result[0]));  // open: SET
  _1bitALU u_1bitalu_2 (
    .A(in_2[1]), .B(in_3[1]), .LESS(1'b0), .A_INVERT(Inputs[3]), .in_3(Inputs[2]),
    .CARRY_IN(n1bitalu_1_carryout), .OPPERATION(Inputs[1:0]), .CARRYOUT(n1bitalu_2_carryout),
    .RESULT(Result[1]));  // open: SET
  _1bitALU u_1bitalu_3 (
    .A(in_2[2]), .B(in_3[2]), .LESS(1'b0), .A_INVERT(Inputs[3]), .in_3(Inputs[2]),
    .CARRY_IN(n1bitalu_2_carryout), .OPPERATION(Inputs[1:0]), .CARRYOUT(n1bitalu_3_carryout),
    .RESULT(Result[2]));  // open: SET
  _1bitALU u_1bitalu_4 (
    .A(in_2[3]), .B(in_3[3]), .LESS(1'b0), .A_INVERT(Inputs[3]), .in_3(Inputs[2]),
    .CARRY_IN(n1bitalu_3_carryout), .OPPERATION(Inputs[1:0]), .CARRYOUT(n1bitalu_4_carryout),
    .RESULT(Result[3]));  // open: SET
  _1bitALU u_1bitalu_5 (
    .A(in_2[4]), .B(in_3[4]), .LESS(1'b0), .A_INVERT(Inputs[3]), .in_3(Inputs[2]),
    .CARRY_IN(n1bitalu_4_carryout), .OPPERATION(Inputs[1:0]), .CARRYOUT(n1bitalu_5_carryout),
    .RESULT(Result[4]));  // open: SET
  _1bitALU u_1bitalu_6 (
    .A(in_2[5]), .B(in_3[5]), .LESS(1'b0), .A_INVERT(Inputs[3]), .in_3(Inputs[2]),
    .CARRY_IN(n1bitalu_5_carryout), .OPPERATION(Inputs[1:0]), .CARRYOUT(n1bitalu_6_carryout),
    .RESULT(Result[5]));  // open: SET
  _1bitALU u_1bitalu_7 (
    .A(in_2[6]), .B(in_3[6]), .LESS(1'b0), .A_INVERT(Inputs[3]), .in_3(Inputs[2]),
    .CARRY_IN(n1bitalu_6_carryout), .OPPERATION(Inputs[1:0]), .CARRYOUT(n1bitalu_7_carryout),
    .RESULT(Result[6]));  // open: SET
  _1bitALU u_1bitalu_8 (
    .A(in_2[7]), .B(in_3[7]), .LESS(1'b0), .A_INVERT(Inputs[3]), .in_3(Inputs[2]),
    .CARRY_IN(n1bitalu_7_carryout), .OPPERATION(Inputs[1:0]), .CARRYOUT(Overflow), .RESULT(Result[7]),
    .SET(n1bitalu_8_set));
  or or_1 (or_1_out, Result[0], Result[1], Result[2], Result[3], Result[4], Result[5], Result[6], Result[7]);
  not not_1 (Zero, or_1_out);

  // Notes on the sheet:
  //   a
  //   b
  //   constant
endmodule
