// Logisim project calculatorCPU-2.circ as structural Verilog: 18 circuits, main circuit main
module main (
);

  wire _0_out, _1_out, _2_out, _3_out, _4_out, _5_out, _6_out, _7_out, _8_out, _9_out, button_2_out,
       button_3_out, button_4_out, button_5_out, button_out, C_out, clock_1_out, keypad_controller_1_write;
  wire [2:0] lcd_controller_1__7_segment_2_2, lcd_controller_1__7_segment_3_2,
       lcd_controller_1__7_segment_4_2, lcd_controller_1__7_segment_5_2, lcd_controller_1__7_segment_6_2,
       lcd_controller_1_minus_2;
  wire [3:0] lcd_controller_1__7_segment_2, lcd_controller_1__7_segment_3, lcd_controller_1__7_segment_4,
       lcd_controller_1__7_segment_5, lcd_controller_1__7_segment_6, lcd_controller_1_minus;
  wire [6:0] lcd_controller_1__7_segment_0, lcd_controller_1__7_segment_1, lcd_controller_1__7_segment_7,
       lcd_controller_1__7_segment_8, lcd_controller_1__7_segment_9;
  wire [31:0] keypad_controller_1_output, processor_1_read_t8, processor_1_read_t9;

  Processor processor_1 (
    .Write_T9(keypad_controller_1_output), .Read_T8(processor_1_read_t8), .Read_T9(processor_1_read_t9),
    .Clock(clock_1_out), .T9_Write_Signal(keypad_controller_1_write));  // open: Clear
  Clock clock_1 (.out(clock_1_out));
  // Probe on processor_1_read_t9
  // Probe on keypad_controller_1_output
  _7_Segment_Display u_7_segment_display_1 (
    .g(lcd_controller_1_minus[0]), .f(lcd_controller_1_minus[1]), .a(lcd_controller_1_minus[2]),
    .b(lcd_controller_1_minus[3]), .e(lcd_controller_1_minus_2[0]), .d(lcd_controller_1_minus_2[1]),
    .c(lcd_controller_1_minus_2[2]));  // open: dp
  LCD_Controller lcd_controller_1 (
    .From__t8(processor_1_read_t8), .Minus({lcd_controller_1_minus_2, lcd_controller_1_minus}),
    ._7_Segment_9(lcd_controller_1__7_segment_9), ._7_Segment_8(lcd_controller_1__7_segment_8),
    ._7_Segment_7(lcd_controller_1__7_segment_7),
    ._7_Segment_6({lcd_controller_1__7_segment_6_2, lcd_controller_1__7_segment_6}),
    ._7_Segment_5({lcd_controller_1__7_segment_5_2, lcd_controller_1__7_segment_5}),
    ._7_Segment_4({lcd_controller_1__7_segment_4_2, lcd_controller_1__7_segment_4}),
    ._7_Segment_3({lcd_controller_1__7_segment_3_2, lcd_controller_1__7_segment_3}),
    ._7_Segment_2({lcd_controller_1__7_segment_2_2, lcd_controller_1__7_segment_2}),
    ._7_Segment_1(lcd_controller_1__7_segment_1), ._7_Segment_0(lcd_controller_1__7_segment_0));
  Keypad_Controller keypad_controller_1 (
    .C(C_out), .in_2(button_out), .in_3(button_5_out), .in_4(button_4_out), .in_5(button_3_out),
    .in_6(button_2_out), ._9(_9_out), ._8(_8_out), ._7(_7_out), ._6(_6_out), ._5(_5_out), ._4(_4_out),
    ._3(_3_out), ._2(_2_out), ._1(_1_out), ._0(_0_out), .From__t9(processor_1_read_t9),
    .Write(keypad_controller_1_write), .Output(keypad_controller_1_output));
  _7_Segment_Display u_7_segment_display_2 (
    .g(lcd_controller_1__7_segment_8[0]), .f(lcd_controller_1__7_segment_8[1]),
    .a(lcd_controller_1__7_segment_8[2]), .b(lcd_controller_1__7_segment_8[3]),
    .e(lcd_controller_1__7_segment_8[4]), .d(lcd_controller_1__7_segment_8[5]),
    .c(lcd_controller_1__7_segment_8[6]));  // open: dp
  _7_Segment_Display u_7_segment_display_3 (
    .g(lcd_controller_1__7_segment_9[0]), .f(lcd_controller_1__7_segment_9[1]),
    .a(lcd_controller_1__7_segment_9[2]), .b(lcd_controller_1__7_segment_9[3]),
    .e(lcd_controller_1__7_segment_9[4]), .d(lcd_controller_1__7_segment_9[5]),
    .c(lcd_controller_1__7_segment_9[6]));  // open: dp
  _7_Segment_Display u_7_segment_display_4 (
    .g(lcd_controller_1__7_segment_7[0]), .f(lcd_controller_1__7_segment_7[1]),
    .a(lcd_controller_1__7_segment_7[2]), .b(lcd_controller_1__7_segment_7[3]),
    .e(lcd_controller_1__7_segment_7[4]), .d(lcd_controller_1__7_segment_7[5]),
    .c(lcd_controller_1__7_segment_7[6]));  // open: dp
  _7_Segment_Display u_7_segment_display_5 (
    .g(lcd_controller_1__7_segment_6[0]), .f(lcd_controller_1__7_segment_6[1]),
    .a(lcd_controller_1__7_segment_6[2]), .b(lcd_controller_1__7_segment_6[3]),
    .e(lcd_controller_1__7_segment_6_2[0]), .d(lcd_controller_1__7_segment_6_2[1]),
    .c(lcd_controller_1__7_segment_6_2[2]));  // open: dp
  _7_Segment_Display u_7_segment_display_6 (
    .g(lcd_controller_1__7_segment_4[0]), .f(lcd_controller_1__7_segment_4[1]),
    .a(lcd_controller_1__7_segment_4[2]), .b(lcd_controller_1__7_segment_4[3]),
    .e(lcd_controller_1__7_segment_4_2[0]), .d(lcd_controller_1__7_segment_4_2[1]),
    .c(lcd_controller_1__7_segment_4_2[2]));  // open: dp
  _7_Segment_Display u_7_segment_display_7 (
    .g(lcd_controller_1__7_segment_5[0]), .f(lcd_controller_1__7_segment_5[1]),
    .a(lcd_controller_1__7_segment_5[2]), .b(lcd_controller_1__7_segment_5[3]),
    .e(lcd_controller_1__7_segment_5_2[0]), .d(lcd_controller_1__7_segment_5_2[1]),
    .c(lcd_controller_1__7_segment_5_2[2]));  // open: dp
  Button _7 (.out(_7_out));
  Button _4 (.out(_4_out));
  Button _1 (.out(_1_out));
  Button _0 (.out(_0_out));
  _7_Segment_Display u_7_segment_display_8 (
    .g(lcd_controller_1__7_segment_3[0]), .f(lcd_controller_1__7_segment_3[1]),
    .a(lcd_controller_1__7_segment_3[2]), .b(lcd_controller_1__7_segment_3[3]),
    .e(lcd_controller_1__7_segment_3_2[0]), .d(lcd_controller_1__7_segment_3_2[1]),
    .c(lcd_controller_1__7_segment_3_2[2]));  // open: dp
  _7_Segment_Display u_7_segment_display_9 (
    .g(lcd_controller_1__7_segment_2[0]), .f(lcd_controller_1__7_segment_2[1]),
    .a(lcd_controller_1__7_segment_2[2]), .b(lcd_controller_1__7_segment_2[3]),
    .e(lcd_controller_1__7_segment_2_2[0]), .d(lcd_controller_1__7_segment_2_2[1]),
    .c(lcd_controller_1__7_segment_2_2[2]));  // open: dp
  Button _9 (.out(_9_out));
  Button _8 (.out(_8_out));
  Button _6 (.out(_6_out));
  Button _5 (.out(_5_out));
  Button _3 (.out(_3_out));
  Button _2 (.out(_2_out));
  Button button (.out(button_out));
  Button C (.out(C_out));
  _7_Segment_Display u_7_segment_display_10 (
    .g(lcd_controller_1__7_segment_0[0]), .f(lcd_controller_1__7_segment_0[1]),
    .a(lcd_controller_1__7_segment_0[2]), .b(lcd_controller_1__7_segment_0[3]),
    .e(lcd_controller_1__7_segment_0[4]), .d(lcd_controller_1__7_segment_0[5]),
    .c(lcd_controller_1__7_segment_0[6]));  // open: dp
  _7_Segment_Display u_7_segment_display_11 (
    .g(lcd_controller_1__7_segment_1[0]), .f(lcd_controller_1__7_segment_1[1]),
    .a(lcd_controller_1__7_segment_1[2]), .b(lcd_controller_1__7_segment_1[3]),
    .e(lcd_controller_1__7_segment_1[4]), .d(lcd_controller_1__7_segment_1[5]),
    .c(lcd_controller_1__7_segment_1[6]));  // open: dp
  Button button_2 (.out(button_2_out));
  Button button_3 (.out(button_3_out));
  Button button_4 (.out(button_4_out));
  Button button_5 (.out(button_5_out));

  // Notes on the sheet:
  //   From $t8
  //   From $t9
  //   Write Data to $t9
  //   Write Signal for $t9
endmodule

module LCD_Controller (
  input  [31:0] From__t8,
  output [6:0] Minus,
  output [6:0] _7_Segment_9,
  output [6:0] _7_Segment_8,
  output [6:0] _7_Segment_7,
  output [6:0] _7_Segment_6,
  output [6:0] _7_Segment_5,
  output [6:0] _7_Segment_4,
  output [6:0] _7_Segment_3,
  output [6:0] _7_Segment_2,
  output [6:0] _7_Segment_1,
  output [6:0] _7_Segment_0
);

  wire [3:0] binarytobcd_1_bcd0, binarytobcd_1_bcd1, binarytobcd_1_bcd2, binarytobcd_1_bcd3,
       binarytobcd_1_bcd4, binarytobcd_1_bcd5, binarytobcd_1_bcd6, binarytobcd_1_bcd7, binarytobcd_1_bcd8,
       binarytobcd_1_bcd9;

  BinaryToBCD binarytobcd_1 (
    .Input(From__t8), .Minus(Minus[0]), .BCD9(binarytobcd_1_bcd9), .BCD8(binarytobcd_1_bcd8),
    .BCD7(binarytobcd_1_bcd7), .BCD6(binarytobcd_1_bcd6), .BCD5(binarytobcd_1_bcd5),
    .BCD4(binarytobcd_1_bcd4), .BCD3(binarytobcd_1_bcd3), .BCD2(binarytobcd_1_bcd2),
    .BCD1(binarytobcd_1_bcd1), .BCD0(binarytobcd_1_bcd0));
  _7_Segment_Controller u_7_segment_controller_1 (.BCD(binarytobcd_1_bcd9), .out_2(_7_Segment_9));
  _7_Segment_Controller u_7_segment_controller_2 (.BCD(binarytobcd_1_bcd8), .out_2(_7_Segment_8));
  _7_Segment_Controller u_7_segment_controller_3 (.BCD(binarytobcd_1_bcd7), .out_2(_7_Segment_7));
  _7_Segment_Controller u_7_segment_controller_4 (.BCD(binarytobcd_1_bcd6), .out_2(_7_Segment_6));
  _7_Segment_Controller u_7_segment_controller_5 (.BCD(binarytobcd_1_bcd5), .out_2(_7_Segment_5));
  _7_Segment_Controller u_7_segment_controller_6 (.BCD(binarytobcd_1_bcd4), .out_2(_7_Segment_4));
  _7_Segment_Controller u_7_segment_controller_7 (.BCD(binarytobcd_1_bcd3), .out_2(_7_Segment_3));
  _7_Segment_Controller u_7_segment_controller_8 (.BCD(binarytobcd_1_bcd2), .out_2(_7_Segment_2));
  _7_Segment_Controller u_7_segment_controller_9 (.BCD(binarytobcd_1_bcd1), .out_2(_7_Segment_1));
  _7_Segment_Controller u_7_segment_controller_10 (.BCD(binarytobcd_1_bcd0), .out_2(_7_Segment_0));

  assign Minus[6:1] = {6{1'b0}};
endmodule

module _7_Segment_Controller (
  input  [3:0] BCD,
  output [6:0] out_2
);

  wire and_1_out, and_2_out, and_3_out, and_4_out, and_5_out, and_6_out, and_7_out, and_8_out, and_9_out,
       and_10_out, and_11_out, and_12_out, and_13_out, and_14_out, and_15_out, and_16_out, not_1_out,
       not_2_out, not_3_out, not_4_out, not_5_out, not_6_out, not_7_out, not_8_out, not_9_out, not_10_out,
       not_11_out, not_12_out, not_13_out, not_14_out, not_15_out, not_16_out, not_17_out, not_18_out,
       not_19_out, not_20_out, not_21_out;

  not not_1 (not_1_out, BCD[2]);
  not not_2 (not_2_out, BCD[0]);
  not not_3 (not_3_out, BCD[1]);
  not not_4 (not_4_out, BCD[1]);
  not not_5 (not_5_out, BCD[0]);
  not not_6 (not_6_out, BCD[1]);
  not not_7 (not_7_out, BCD[0]);
  not not_8 (not_8_out, BCD[2]);
  not not_9 (not_9_out, BCD[0]);
  not not_10 (not_10_out, BCD[1]);
  not not_11 (not_11_out, BCD[0]);
  not not_12 (not_12_out, BCD[2]);
  not not_13 (not_13_out, BCD[0]);
  not not_14 (not_14_out, BCD[0]);
  not not_15 (not_15_out, BCD[2]);
  not not_16 (not_16_out, BCD[0]);
  not not_17 (not_17_out, BCD[2]);
  not not_18 (not_18_out, BCD[0]);
  not not_19 (not_19_out, BCD[1]);
  not not_20 (not_20_out, BCD[1]);
  and and_1 (and_1_out, not_1_out, BCD[1]);
  and and_2 (and_2_out, BCD[1], not_2_out);
  and and_3 (and_3_out, BCD[2], not_3_out);
  and and_4 (and_4_out, not_4_out, not_5_out);
  and and_5 (and_5_out, BCD[2], not_6_out);
  and and_6 (and_6_out, BCD[2], not_7_out);
  and and_7 (and_7_out, not_8_out, not_9_out);
  and and_8 (and_8_out, BCD[2], BCD[0]);
  not not_21 (not_21_out, BCD[2]);
  and and_9 (and_9_out, not_10_out, not_11_out);
  and and_10 (and_10_out, BCD[1], BCD[0]);
  and and_11 (and_11_out, not_12_out, not_13_out);
  and and_12 (and_12_out, BCD[1], not_14_out);
  and and_13 (and_13_out, not_15_out, not_16_out);
  and and_14 (and_14_out, not_17_out, BCD[1]);
  and and_15 (and_15_out, BCD[1], not_18_out);
  and and_16 (and_16_out, BCD[2], not_19_out, BCD[0]);
  or or_1 (out_2[6], not_20_out, BCD[0], BCD[2]);
  or or_2 (out_2[0], and_1_out, and_2_out, and_3_out, BCD[3]);
  or or_3 (out_2[1], and_4_out, and_5_out, and_6_out, BCD[3]);
  or or_4 (out_2[2], and_7_out, BCD[1], and_8_out, BCD[3]);
  or or_5 (out_2[3], not_21_out, and_9_out, and_10_out);
  or or_6 (out_2[4], and_11_out, and_12_out);
  or or_7 (out_2[5], and_13_out, and_14_out, and_15_out, and_16_out);
endmodule

module BinaryToBCD (
  input  [31:0] Input,
  output Minus,
  output [3:0] BCD9,
  output [3:0] BCD8,
  output [3:0] BCD7,
  output [3:0] BCD6,
  output [3:0] BCD5,
  output [3:0] BCD4,
  output [3:0] BCD3,
  output [3:0] BCD2,
  output [3:0] BCD1,
  output [3:0] BCD0
);

  wire [27:0] subtractor_1_out, subtractor_2_out, subtractor_3_out, subtractor_4_out, subtractor_5_out,
       subtractor_6_out, subtractor_7_out, subtractor_8_out, subtractor_9_out;
  wire [31:0] adder_1_out, divider_1_out, divider_2_out, divider_3_out, divider_4_out, divider_5_out,
       divider_6_out, divider_7_out, divider_8_out, multiplexer_1_out, multiplier_1_out, multiplier_2_out,
       multiplier_3_out, multiplier_4_out, multiplier_5_out, multiplier_6_out, multiplier_7_out,
       multiplier_8_out, multiplier_9_out, not_1_out;
  wire [31:4] divider_9_out;

  assign not_1_out = ~Input;  // NOT_Gate not_1, 32 bits wide
  Adder #(.width(32)) adder_1 (.a(not_1_out), .b(32'h1), .out(adder_1_out));  // open: cin, cout
  Multiplexer #(.width(32)) multiplexer_1 (
    .in0(Input), .in1(adder_1_out), .out(multiplexer_1_out), .sel(Input[31]));  // open: en
  Subtractor #(.width(32)) subtractor_1 (
    .a(multiplexer_1_out), .b(multiplier_1_out), .out({subtractor_1_out, BCD0}));  // open: bin, bout
  Multiplier #(.width(32)) multiplier_1 (.a(divider_1_out), .b(32'ha), .out(multiplier_1_out));  // open: cin, cout
  Divider #(.width(32)) divider_1 (.a(multiplexer_1_out), .b(32'ha), .out(divider_1_out));  // open: upper, rem
  Subtractor #(.width(32)) subtractor_2 (
    .a(divider_1_out), .b(multiplier_2_out), .out({subtractor_2_out, BCD1}));  // open: bin, bout
  Multiplier #(.width(32)) multiplier_2 (.a(divider_2_out), .b(32'ha), .out(multiplier_2_out));  // open: cin, cout
  Divider #(.width(32)) divider_2 (.a(divider_1_out), .b(32'ha), .out(divider_2_out));  // open: upper, rem
  Subtractor #(.width(32)) subtractor_3 (
    .a(divider_2_out), .b(multiplier_3_out), .out({subtractor_3_out, BCD2}));  // open: bin, bout
  Multiplier #(.width(32)) multiplier_3 (.a(divider_3_out), .b(32'ha), .out(multiplier_3_out));  // open: cin, cout
  Divider #(.width(32)) divider_3 (.a(divider_2_out), .b(32'ha), .out(divider_3_out));  // open: upper, rem
  Subtractor #(.width(32)) subtractor_4 (
    .a(divider_3_out), .b(multiplier_4_out), .out({subtractor_4_out, BCD3}));  // open: bin, bout
  Multiplier #(.width(32)) multiplier_4 (.a(divider_4_out), .b(32'ha), .out(multiplier_4_out));  // open: cin, cout
  Divider #(.width(32)) divider_4 (.a(divider_3_out), .b(32'ha), .out(divider_4_out));  // open: upper, rem
  Subtractor #(.width(32)) subtractor_5 (
    .a(divider_4_out), .b(multiplier_5_out), .out({subtractor_5_out, BCD4}));  // open: bin, bout
  Multiplier #(.width(32)) multiplier_5 (.a(divider_5_out), .b(32'ha), .out(multiplier_5_out));  // open: cin, cout
  Divider #(.width(32)) divider_5 (.a(divider_4_out), .b(32'ha), .out(divider_5_out));  // open: upper, rem
  Subtractor #(.width(32)) subtractor_6 (
    .a(divider_5_out), .b(multiplier_6_out), .out({subtractor_6_out, BCD5}));  // open: bin, bout
  Multiplier #(.width(32)) multiplier_6 (.a(divider_6_out), .b(32'ha), .out(multiplier_6_out));  // open: cin, cout
  Divider #(.width(32)) divider_6 (.a(divider_5_out), .b(32'ha), .out(divider_6_out));  // open: upper, rem
  Subtractor #(.width(32)) subtractor_7 (
    .a(divider_6_out), .b(multiplier_7_out), .out({subtractor_7_out, BCD6}));  // open: bin, bout
  Multiplier #(.width(32)) multiplier_7 (.a(divider_7_out), .b(32'ha), .out(multiplier_7_out));  // open: cin, cout
  Divider #(.width(32)) divider_7 (.a(divider_6_out), .b(32'ha), .out(divider_7_out));  // open: upper, rem
  Subtractor #(.width(32)) subtractor_8 (
    .a(divider_7_out), .b(multiplier_8_out), .out({subtractor_8_out, BCD7}));  // open: bin, bout
  Multiplier #(.width(32)) multiplier_8 (.a(divider_8_out), .b(32'ha), .out(multiplier_8_out));  // open: cin, cout
  Divider #(.width(32)) divider_8 (.a(divider_7_out), .b(32'ha), .out(divider_8_out));  // open: upper, rem
  Subtractor #(.width(32)) subtractor_9 (
    .a(divider_8_out), .b(multiplier_9_out), .out({subtractor_9_out, BCD8}));  // open: bin, bout
  Multiplier #(.width(32)) multiplier_9 (
    .a({divider_9_out, BCD9}), .b(32'ha), .out(multiplier_9_out));  // open: cin, cout
  Divider #(.width(32)) divider_9 (.a(divider_8_out), .b(32'ha), .out({divider_9_out, BCD9}));  // open: upper, rem

  assign Minus = Input[31];
endmodule

module Keypad_Controller (
  input  C,
  input  in_2,
  input  in_3,
  input  in_4,
  input  in_5,
  input  in_6,
  input  _9,
  input  _8,
  input  _7,
  input  _6,
  input  _5,
  input  _4,
  input  _3,
  input  _2,
  input  _1,
  input  _0,
  input  [31:0] From__t9,
  output Write,
  output [31:0] Output
);

  wire iszero_1_out_2, iszero_2_out_2;
  wire [3:0] or_4_out;
  wire [15:0] and_16_out;

  and and_1 (and_16_out[1], iszero_1_out_2, in_2);
  and and_2 (and_16_out[2], iszero_1_out_2, in_3);
  and and_3 (and_16_out[3], iszero_1_out_2, in_4);
  and and_4 (and_16_out[4], iszero_1_out_2, in_5);
  and and_5 (and_16_out[5], iszero_1_out_2, in_6);
  and and_6 (and_16_out[6], iszero_1_out_2, _9);
  and and_7 (and_16_out[7], iszero_1_out_2, _8);
  and and_8 (and_16_out[8], iszero_1_out_2, _7);
  and and_9 (and_16_out[9], iszero_1_out_2, _6);
  and and_10 (and_16_out[10], iszero_1_out_2, _5);
  and and_11 (and_16_out[11], iszero_1_out_2, _4);
  and and_12 (and_16_out[12], iszero_1_out_2, _3);
  and and_13 (and_16_out[13], iszero_1_out_2, _2);
  and and_14 (and_16_out[14], iszero_1_out_2, _1);
  and and_15 (and_16_out[15], iszero_1_out_2, _0);
  isZero iszero_1 (.Input(From__t9), .out_2(iszero_1_out_2));
  and and_16 (and_16_out[0], iszero_1_out_2, C);
  or or_1 (or_4_out[3], and_16_out[0], and_16_out[1], and_16_out[2], and_16_out[3], and_16_out[4], and_16_out[5], and_16_out[6], and_16_out[7]);
  or or_2 (or_4_out[2], and_16_out[8], and_16_out[9], and_16_out[10], and_16_out[11], and_16_out[0], and_16_out[1], and_16_out[2], and_16_out[3]);
  or or_3 (or_4_out[1], and_16_out[12], and_16_out[13], and_16_out[9], and_16_out[8], and_16_out[5], and_16_out[4], and_16_out[1], and_16_out[0]);
  or or_4 (or_4_out[0], and_16_out[12], and_16_out[14], and_16_out[10], and_16_out[8], and_16_out[6], and_16_out[4], and_16_out[2], and_16_out[0]);
  isZero iszero_2 (.Input({{16{1'b0}}, and_16_out}), .out_2(iszero_2_out_2));
  not not_1 (Write, iszero_2_out_2);
  assign Output = Write ? {28'h8000000, or_4_out} : 32'bz;  // Controlled_Buffer controlled_buffer_1
endmodule

module isZero (
  input  [31:0] Input,
  output out_2
);

  wire or_1_out;

  not not_1 (out_2, or_1_out);
  or or_1 (or_1_out, Input[0], Input[1], Input[2], Input[3], Input[4], Input[5], Input[6], Input[7], Input[8], Input[9], Input[10], Input[11], Input[12], Input[13], Input[14], Input[15], Input[16], Input[17], Input[18], Input[19], Input[20], Input[21], Input[22], Input[23], Input[24], Input[25], Input[26], Input[27], Input[28], Input[29], Input[30], Input[31]);
endmodule

// MEM
module Instruction_Memory (
  input  [31:0] PC,
  output [31:0] Data
);

  ROM #(.addrWidth(16), .dataWidth(32)) rom_1 (.addr(PC[17:2]), .data(Data));  // open: sel

  // Notes on the sheet:
  //   contents of rom_1 (hex, n*v repeats v):
  //   20190000 20180000 20080000 20090000 200a0000 200b0000 20180000 1320ffff 19c840 19c842 2b31000a
  //   12200008 86840 870c0 1ae4020 c020 3284020 21180000 20190000 8100007 2001000a 1039000a 2001000b
  //   1039000b 2001000c 1039000c 2001000d 1039000d 2001000e 1039000e 2001000f 1039ffe0 200a000a 20190000
  //   8100030 200a000b 20190000 8100030 200a000c 20190000 8100030 200a000d 20190000 8100030 200a000e
  //   1005820 160c020 8100099 1320ffff 19c840 19c842 2b31000a 12200008 96840 970c0 1ae4820 c020 3294820
  //   21380000 20190000 810004d 2001000a 1039000a 2001000b 10390008 2001000c 10390006 2001000d 10390004
  //   2001000e 1039ffe5 2001000f 1039ffb7 3205020 20190000 100c020 8100030 1320ffff 19c840 19c842 2b31000a
  //   12200008 96840 970c0 1ae4820 c020 3294820 21380000 20190000 810004d 2001000a 1039000a 2001000b
  //   10390008 2001000c 10390006 2001000d 10390004 2001000e 10390002 2001000f 1039ff9a 20150000 20160000
  //   2001000c 102a0006 2001000d 102a0008 2001000a 102a001b 2001000b 102a001b 1685820 22b50001 16a9fffd
  //   810008d 29170000 20010001 10370007 1094022 29160000 16c00013 216b0001 29160001 16c00010 8100077
  //   2017ffff 1094020 8702a 20010000 1436000a 20010001 1615822 2e8b02a 20010000 14360005 810007e 1095820
  //   810008d 1095822 810008d 160c020 2001000e 10390005 21680000 5820 4820 3205020 8100031 5020 4820 c820
  //   8100099 1320ffff 19c840 19c842 2b31000a 12200005 c020 3284020 21180000 20190000 8100007 2001000e
  //   10390007 2001000f 1039ff59 1604020 5820 4820 3205020 8100030 160c020 20090000 5820 c820 8100099
endmodule

module Shift_Left (
  input  [31:0] \input ,
  input  [4:0] shamt,
  output [31:0] out_3
);

  wire [31:0] decoder_1_out0;

  Decoder #(.select(5), .enable("false")) decoder_1 (
    .out0(decoder_1_out0[0]), .out1(decoder_1_out0[1]), .out2(decoder_1_out0[2]), .out3(decoder_1_out0[3]),
    .out4(decoder_1_out0[4]), .out5(decoder_1_out0[5]), .out6(decoder_1_out0[6]), .out7(decoder_1_out0[7]),
    .out8(decoder_1_out0[8]), .out9(decoder_1_out0[9]), .out10(decoder_1_out0[10]),
    .out11(decoder_1_out0[11]), .out12(decoder_1_out0[12]), .out13(decoder_1_out0[13]),
    .out14(decoder_1_out0[14]), .out15(decoder_1_out0[15]), .out16(decoder_1_out0[16]),
    .out17(decoder_1_out0[17]), .out18(decoder_1_out0[18]), .out19(decoder_1_out0[19]),
    .out20(decoder_1_out0[20]), .out21(decoder_1_out0[21]), .out22(decoder_1_out0[22]),
    .out23(decoder_1_out0[23]), .out24(decoder_1_out0[24]), .out25(decoder_1_out0[25]),
    .out26(decoder_1_out0[26]), .out27(decoder_1_out0[27]), .out28(decoder_1_out0[28]),
    .out29(decoder_1_out0[29]), .out30(decoder_1_out0[30]), .out31(decoder_1_out0[31]), .sel(shamt));
  Multiplier #(.width(32)) multiplier_1 (.a(\input ), .b(decoder_1_out0), .out(out_3));  // open: cin, cout
endmodule

module Shift_Right (
  input  [31:0] \input ,
  input  [4:0] shamt,
  output [31:0] out_3
);

  wire [31:0] decoder_1_out0;

  Decoder #(.select(5), .enable("false")) decoder_1 (
    .out0(decoder_1_out0[0]), .out1(decoder_1_out0[1]), .out2(decoder_1_out0[2]), .out3(decoder_1_out0[3]),
    .out4(decoder_1_out0[4]), .out5(decoder_1_out0[5]), .out6(decoder_1_out0[6]), .out7(decoder_1_out0[7]),
    .out8(decoder_1_out0[8]), .out9(decoder_1_out0[9]), .out10(decoder_1_out0[10]),
    .out11(decoder_1_out0[11]), .out12(decoder_1_out0[12]), .out13(decoder_1_out0[13]),
    .out14(decoder_1_out0[14]), .out15(decoder_1_out0[15]), .out16(decoder_1_out0[16]),
    .out17(decoder_1_out0[17]), .out18(decoder_1_out0[18]), .out19(decoder_1_out0[19]),
    .out20(decoder_1_out0[20]), .out21(decoder_1_out0[21]), .out22(decoder_1_out0[22]),
    .out23(decoder_1_out0[23]), .out24(decoder_1_out0[24]), .out25(decoder_1_out0[25]),
    .out26(decoder_1_out0[26]), .out27(decoder_1_out0[27]), .out28(decoder_1_out0[28]),
    .out29(decoder_1_out0[29]), .out30(decoder_1_out0[30]), .out31(decoder_1_out0[31]), .sel(shamt));
  Divider #(.width(32)) divider_1 (.a(\input ), .b(decoder_1_out0), .out(out_3));  // open: upper, rem
endmodule

module Sign_Extend (
  input  [15:0] in,
  output [31:0] out
);


  assign out = {{17{in[15]}}, in[14:0]};
endmodule

// ALU
module _32_bit_ALU (
  input  [1:0] SHFTOP,
  input  [3:0] ALUOP,
  input  [31:0] A,
  input  [31:0] B,
  input  [4:0] shamt,
  output [31:0] Result,
  output Zero
);

  wire [31:0] adder_1_out, and_1_out, multiplexer_1_out, multiplexer_2_out, multiplexer_3_out, not_1_out,
       not_2_out, or_1_out, shift_left_1_out_3, shift_right_1_out_3;

  assign not_1_out = ~A;  // NOT_Gate not_1, 32 bits wide
  assign not_2_out = ~B;  // NOT_Gate not_2, 32 bits wide
  Multiplexer #(.width(32), .enable("false")) multiplexer_1 (
    .in0(A), .in1(not_1_out), .out(multiplexer_1_out), .sel(ALUOP[3]));
  Multiplexer #(.width(32), .enable("false")) multiplexer_2 (
    .in0(B), .in1(not_2_out), .out(multiplexer_2_out), .sel(ALUOP[2]));
  Shift_Left shift_left_1 (.\input (B), .shamt(shamt), .out_3(shift_left_1_out_3));
  Shift_Right shift_right_1 (.\input (B), .shamt(shamt), .out_3(shift_right_1_out_3));
  assign and_1_out = multiplexer_1_out & multiplexer_2_out;  // AND_Gate and_1, 32 bits wide
  assign or_1_out = multiplexer_1_out | multiplexer_2_out;  // OR_Gate or_1, 32 bits wide
  Adder #(.width(32)) adder_1 (
    .a(multiplexer_1_out), .b(multiplexer_2_out), .out(adder_1_out), .cin(ALUOP[2]));  // open: cout
  Multiplexer #(.select(2), .width(32), .enable("false")) multiplexer_3 (
    .in0(and_1_out), .in1(or_1_out), .in2(adder_1_out), .in3({{31{1'b0}}, adder_1_out[31]}),
    .out(multiplexer_3_out), .sel(ALUOP[1:0]));
  Multiplexer #(.select(2), .width(32), .enable("false")) multiplexer_4 (
    .in0(multiplexer_3_out), .in2(shift_left_1_out_3), .in3(shift_right_1_out_3), .out(Result), .sel(SHFTOP));  // open: in1
  isZero iszero_1 (.Input(Result), .out_2(Zero));
endmodule

// REG
module Register_File (
  input  [4:0] ReadRegister1,
  input  RegWrite,
  input  Clock,
  input  [31:0] WriteData,
  input  [4:0] ReadRegister2,
  input  [4:0] WriteRegister,
  input  [31:0] T9WriteData,
  input  T9WriteSignal,
  input  clear,
  output [31:0] ReadData1,
  output [31:0] ReadData2,
  output [31:0] T8Data,
  output [31:0] T9Data
);

  wire buffer_1_out, demultiplexer_1_out1, demultiplexer_1_out2, demultiplexer_1_out3, demultiplexer_1_out4,
       demultiplexer_1_out5, demultiplexer_1_out6, demultiplexer_1_out7, demultiplexer_1_out8,
       demultiplexer_1_out9, demultiplexer_1_out10, demultiplexer_1_out11, demultiplexer_1_out12,
       demultiplexer_1_out13, demultiplexer_1_out14, demultiplexer_1_out15, demultiplexer_1_out16,
       demultiplexer_1_out17, demultiplexer_1_out18, demultiplexer_1_out19, demultiplexer_1_out20,
       demultiplexer_1_out21, demultiplexer_1_out22, demultiplexer_1_out23, demultiplexer_1_out24,
       demultiplexer_1_out25, demultiplexer_1_out26, demultiplexer_1_out27, demultiplexer_1_out28,
       demultiplexer_1_out29, demultiplexer_1_out30, demultiplexer_1_out31;
  wire [31:0] controlled_buffer_1_out, register_1_q, register_2_q, register_3_q, register_4_q, register_5_q,
       register_6_q, register_7_q, register_8_q, register_9_q, register_10_q, register_11_q, register_12_q,
       register_13_q, register_14_q, register_15_q, register_16_q, register_17_q, register_18_q,
       register_19_q, register_20_q, register_21_q, register_22_q, register_23_q, register_24_q,
       register_27_q, register_28_q, register_29_q, register_30_q, register_31_q, register_32_q;

  assign controlled_buffer_1_out = T9WriteSignal ? T9WriteData : 32'bz;  // Controlled_Buffer controlled_buffer_1
  buf buffer_1 (buffer_1_out, T9WriteSignal);
  Demultiplexer #(.select(5), .enable("false")) demultiplexer_1 (
    .out1(demultiplexer_1_out1), .out2(demultiplexer_1_out2), .out3(demultiplexer_1_out3),
    .out4(demultiplexer_1_out4), .out5(demultiplexer_1_out5), .out6(demultiplexer_1_out6),
    .out7(demultiplexer_1_out7), .out8(demultiplexer_1_out8), .out9(demultiplexer_1_out9),
    .out10(demultiplexer_1_out10), .out11(demultiplexer_1_out11), .out12(demultiplexer_1_out12),
    .out13(demultiplexer_1_out13), .out14(demultiplexer_1_out14), .out15(demultiplexer_1_out15),
    .out16(demultiplexer_1_out16), .out17(demultiplexer_1_out17), .out18(demultiplexer_1_out18),
    .out19(demultiplexer_1_out19), .out20(demultiplexer_1_out20), .out21(demultiplexer_1_out21),
    .out22(demultiplexer_1_out22), .out23(demultiplexer_1_out23), .out24(demultiplexer_1_out24),
    .out25(demultiplexer_1_out25), .out26(demultiplexer_1_out26), .out27(demultiplexer_1_out27),
    .out28(demultiplexer_1_out28), .out29(demultiplexer_1_out29), .out30(demultiplexer_1_out30),
    .out31(demultiplexer_1_out31), .in(RegWrite), .sel(WriteRegister));  // open: out0
  assign controlled_buffer_1_out = demultiplexer_1_out25 ? WriteData : 32'bz;  // Controlled_Buffer controlled_buffer_2
  buf buffer_2 (buffer_1_out, demultiplexer_1_out25);
  Register #(.width(32)) register_1 (.D(WriteData), .en(1'b0), .Q(register_1_q), .clk(Clock), .clr(clear));
  Register #(.width(32)) register_2 (
    .D(WriteData), .en(demultiplexer_1_out1), .Q(register_2_q), .clk(Clock), .clr(clear));
  Register #(.width(32)) register_3 (
    .D(WriteData), .en(demultiplexer_1_out2), .Q(register_3_q), .clk(Clock), .clr(clear));
  Register #(.width(32)) register_4 (
    .D(WriteData), .en(demultiplexer_1_out3), .Q(register_4_q), .clk(Clock), .clr(clear));
  Register #(.width(32)) register_5 (
    .D(WriteData), .en(demultiplexer_1_out4), .Q(register_5_q), .clk(Clock), .clr(clear));
  Register #(.width(32)) register_6 (
    .D(WriteData), .en(demultiplexer_1_out5), .Q(register_6_q), .clk(Clock), .clr(clear));
  Register #(.width(32)) register_7 (
    .D(WriteData), .en(demultiplexer_1_out6), .Q(register_7_q), .clk(Clock), .clr(clear));
  Register #(.width(32)) register_8 (
    .D(WriteData), .en(demultiplexer_1_out7), .Q(register_8_q), .clk(Clock), .clr(clear));
  Register #(.width(32)) register_9 (
    .D(WriteData), .en(demultiplexer_1_out8), .Q(register_9_q), .clk(Clock), .clr(clear));
  Register #(.width(32)) register_10 (
    .D(WriteData), .en(demultiplexer_1_out9), .Q(register_10_q), .clk(Clock), .clr(clear));
  Register #(.width(32)) register_11 (
    .D(WriteData), .en(demultiplexer_1_out10), .Q(register_11_q), .clk(Clock), .clr(clear));
  Register #(.width(32)) register_12 (
    .D(WriteData), .en(demultiplexer_1_out11), .Q(register_12_q), .clk(Clock), .clr(clear));
  Register #(.width(32)) register_13 (
    .D(WriteData), .en(demultiplexer_1_out12), .Q(register_13_q), .clk(Clock), .clr(clear));
  Register #(.width(32)) register_14 (
    .D(WriteData), .en(demultiplexer_1_out13), .Q(register_14_q), .clk(Clock), .clr(clear));
  Register #(.width(32)) register_15 (
    .D(WriteData), .en(demultiplexer_1_out14), .Q(register_15_q), .clk(Clock), .clr(clear));
  Register #(.width(32)) register_16 (
    .D(WriteData), .en(demultiplexer_1_out15), .Q(register_16_q), .clk(Clock), .clr(clear));
  Register #(.width(32)) register_17 (
    .D(WriteData), .en(demultiplexer_1_out16), .Q(register_17_q), .clk(Clock), .clr(clear));
  Register #(.width(32)) register_18 (
    .D(WriteData), .en(demultiplexer_1_out17), .Q(register_18_q), .clk(Clock), .clr(clear));
  Register #(.width(32)) register_19 (
    .D(WriteData), .en(demultiplexer_1_out18), .Q(register_19_q), .clk(Clock), .clr(clear));
  Register #(.width(32)) register_20 (
    .D(WriteData), .en(demultiplexer_1_out19), .Q(register_20_q), .clk(Clock), .clr(clear));
  Register #(.width(32)) register_21 (
    .D(WriteData), .en(demultiplexer_1_out20), .Q(register_21_q), .clk(Clock), .clr(clear));
  Register #(.width(32)) register_22 (
    .D(WriteData), .en(demultiplexer_1_out21), .Q(register_22_q), .clk(Clock), .clr(clear));
  Register #(.width(32)) register_23 (
    .D(WriteData), .en(demultiplexer_1_out22), .Q(register_23_q), .clk(Clock), .clr(clear));
  Register #(.width(32)) register_24 (
    .D(WriteData), .en(demultiplexer_1_out23), .Q(register_24_q), .clk(Clock), .clr(clear));
  Register #(.width(32)) register_25 (.D(WriteData), .en(demultiplexer_1_out24), .Q(T8Data), .clk(Clock), .clr(clear));
  Register #(.width(32)) register_26 (
    .D(controlled_buffer_1_out), .en(buffer_1_out), .Q(T9Data), .clk(Clock), .clr(clear));
  Register #(.width(32)) register_27 (
    .D(WriteData), .en(demultiplexer_1_out26), .Q(register_27_q), .clk(Clock), .clr(clear));
  Register #(.width(32)) register_28 (
    .D(WriteData), .en(demultiplexer_1_out27), .Q(register_28_q), .clk(Clock), .clr(clear));
  Register #(.width(32)) register_29 (
    .D(WriteData), .en(demultiplexer_1_out28), .Q(register_29_q), .clk(Clock), .clr(clear));
  Register #(.width(32)) register_30 (
    .D(WriteData), .en(demultiplexer_1_out29), .Q(register_30_q), .clk(Clock), .clr(clear));
  Register #(.width(32)) register_31 (
    .D(WriteData), .en(demultiplexer_1_out30), .Q(register_31_q), .clk(Clock), .clr(clear));
  Register #(.width(32)) register_32 (
    .D(WriteData), .en(demultiplexer_1_out31), .Q(register_32_q), .clk(Clock), .clr(clear));
  Multiplexer #(.select(5), .width(32), .enable("false")) multiplexer_1 (
    .in0(register_1_q), .in1(register_2_q), .in2(register_3_q), .in3(register_4_q), .in4(register_5_q),
    .in5(register_6_q), .in6(register_7_q), .in7(register_8_q), .in8(register_9_q), .in9(register_10_q),
    .in10(register_11_q), .in11(register_12_q), .in12(register_13_q), .in13(register_14_q),
    .in14(register_15_q), .in15(register_16_q), .in16(register_17_q), .in17(register_18_q),
    .in18(register_19_q), .in19(register_20_q), .in20(register_21_q), .in21(register_22_q),
    .in22(register_23_q), .in23(register_24_q), .in24(T8Data), .in25(T9Data), .in26(register_27_q),
    .in27(register_28_q), .in28(register_29_q), .in29(register_30_q), .in30(register_31_q),
    .in31(register_32_q), .out(ReadData2), .sel(ReadRegister2));
  Multiplexer #(.select(5), .width(32), .enable("false")) multiplexer_2 (
    .in0(register_1_q), .in1(register_2_q), .in2(register_3_q), .in3(register_4_q), .in4(register_5_q),
    .in5(register_6_q), .in6(register_7_q), .in7(register_8_q), .in8(register_9_q), .in9(register_10_q),
    .in10(register_11_q), .in11(register_12_q), .in12(register_13_q), .in13(register_14_q),
    .in14(register_15_q), .in15(register_16_q), .in16(register_17_q), .in17(register_18_q),
    .in18(register_19_q), .in19(register_20_q), .in20(register_21_q), .in21(register_22_q),
    .in22(register_23_q), .in23(register_24_q), .in24(T8Data), .in25(T9Data), .in26(register_27_q),
    .in27(register_28_q), .in28(register_29_q), .in29(register_30_q), .in30(register_31_q),
    .in31(register_32_q), .out(ReadData1), .sel(ReadRegister1));

  // Notes on the sheet:
  //   buffer_1 drives only 1 and floats otherwise
  //   buffer_2 drives only 1 and floats otherwise
endmodule

// CU
module Control_Unit (
  input  [5:0] OP,
  input  [5:0] FN,
  output RegDest,
  output Jump,
  output Branch,
  output [3:0] out_6,
  output [1:0] SHFTOp,
  output ALUSrc,
  output RegWrite,
  output InvZero
);

  wire not_1_out, not_2_out, not_3_out, not_4_out, not_5_out, not_7_out, not_8_out, not_9_out, not_10_out,
       not_11_out, or_1_out, or_2_out;
  wire [1:0] and_4_out;

  or or_1 (or_1_out, OP[0], OP[3], OP[2], OP[4], OP[5], OP[1]);
  not not_1 (not_1_out, OP[3]);
  not not_2 (not_2_out, OP[2]);
  not not_3 (not_3_out, OP[0]);
  not not_4 (not_4_out, OP[3]);
  not not_5 (not_5_out, OP[1]);
  not not_6 (RegDest, or_2_out);
  or or_2 (or_2_out, OP[5], OP[4], OP[3], OP[2], OP[1], OP[0]);
  and and_1 (Jump, not_1_out, not_2_out, OP[1], not_3_out);
  and and_2 (Branch, not_4_out, OP[2], not_5_out);
  ALUOPGen aluopgen_1 (
    .Opp3(OP[3]), .Opp2(OP[2]), .Opp1(OP[1]), .Opp0(OP[0]), .funct5(FN[5]), .funct3(FN[3]), .funct2(FN[2]),
    .funct1(FN[1]), .funct0(FN[0]), .ALUOP3(out_6[3]), .ALUOP2(out_6[2]), .ALUOP1(out_6[1]), .ALUOP0(out_6[0]));
  not not_7 (not_7_out, Branch);
  not not_8 (not_8_out, Jump);
  and and_3 (InvZero, Branch, not_9_out);
  not not_9 (not_9_out, OP[0]);
  not not_10 (not_10_out, or_1_out);
  and and_4 (and_4_out[0], not_11_out, FN[1]);
  not not_11 (not_11_out, FN[5]);
  and and_5 (RegWrite, not_7_out, not_8_out);
  not not_12 (and_4_out[1], FN[5]);
  Multiplexer #(.width(2)) multiplexer_1 (.in0(2'b00), .in1(and_4_out), .out(SHFTOp), .sel(not_10_out));  // open: en

  assign ALUSrc = OP[3];
endmodule

module Shift_Left_Two (
  input  [31:0] Input,
  output [31:0] out_2
);


  assign out_2 = {Input[29:0], 2'b00};
endmodule

module Processor (
  input  Clock,
  input  Clear,
  input  [31:0] Write_T9,
  input  T9_Write_Signal,
  output [31:0] Read_T8,
  output [31:0] Read_T9
);

  wire and_1_out, control_unit_1_alusrc, control_unit_1_branch, control_unit_1_invzero, control_unit_1_jump,
       control_unit_1_regdest, control_unit_1_regwrite, n32_bit_alu_1_zero, xnor_1_out;
  wire [1:0] control_unit_1_shftop;
  wire [3:0] control_unit_1_out_6;
  wire [4:0] multiplexer_1_out;
  wire [27:0] shift_left_2_jump_1_out;
  wire [31:0] adder_1_out, adder_2_out, instruction_memory_1_data, multiplexer_2_out, multiplexer_3_out,
       multiplexer_4_out, n32_bit_alu_1_result, PC_q, register_file_1_readdata1, register_file_1_readdata2,
       shift_left_two_1_out_2, sign_extend_1_out;

  // Probe on instruction_memory_1_data
  Register #(.width(32)) PC (.D(multiplexer_4_out), .Q(PC_q), .clk(Clock), .clr(Clear));  // open: en
  Instruction_Memory instruction_memory_1 (.PC(PC_q), .Data(instruction_memory_1_data));
  Adder #(.width(32)) adder_1 (.a(32'h4), .b(PC_q), .out(adder_1_out));  // open: cin, cout
  // Probe on instruction_memory_1_data[25:0]
  // Probe on instruction_memory_1_data[31:26]
  // Probe on instruction_memory_1_data[15:0]
  Shift_Left_2_Jump shift_left_2_jump_1 (.in(instruction_memory_1_data[25:0]), .out(shift_left_2_jump_1_out));
  Control_Unit control_unit_1 (
    .OP(instruction_memory_1_data[31:26]), .FN(instruction_memory_1_data[5:0]),
    .RegDest(control_unit_1_regdest), .Jump(control_unit_1_jump), .Branch(control_unit_1_branch),
    .out_6(control_unit_1_out_6), .SHFTOp(control_unit_1_shftop), .ALUSrc(control_unit_1_alusrc),
    .RegWrite(control_unit_1_regwrite), .InvZero(control_unit_1_invzero));
  // Probe on instruction_memory_1_data[5:0]
  Multiplexer #(.width(5)) multiplexer_1 (
    .in0(instruction_memory_1_data[20:16]), .in1(instruction_memory_1_data[15:11]), .out(multiplexer_1_out),
    .sel(control_unit_1_regdest));  // open: en
  Register_File register_file_1 (
    .ReadRegister1(instruction_memory_1_data[25:21]), .WriteData(n32_bit_alu_1_result),
    .ReadRegister2(instruction_memory_1_data[20:16]), .WriteRegister(multiplexer_1_out),
    .T9WriteData(Write_T9), .T9WriteSignal(T9_Write_Signal), .ReadData1(register_file_1_readdata1),
    .ReadData2(register_file_1_readdata2), .T8Data(Read_T8), .T9Data(Read_T9),
    .RegWrite(control_unit_1_regwrite), .Clock(Clock), .clear(Clear));
  Sign_Extend sign_extend_1 (.in(instruction_memory_1_data[15:0]), .out(sign_extend_1_out));
  // Probe on control_unit_1_out_6
  _32_bit_ALU u_32_bit_alu_1 (
    .A(register_file_1_readdata1), .B(multiplexer_2_out), .shamt(instruction_memory_1_data[10:6]),
    .ALUOP(control_unit_1_out_6), .SHFTOP(control_unit_1_shftop), .Result(n32_bit_alu_1_result),
    .Zero(n32_bit_alu_1_zero));
  Multiplexer #(.width(32)) multiplexer_2 (
    .in0(register_file_1_readdata2), .in1(sign_extend_1_out), .out(multiplexer_2_out),
    .sel(control_unit_1_alusrc));  // open: en
  Adder #(.width(32)) adder_2 (.a(adder_1_out), .b(shift_left_two_1_out_2), .out(adder_2_out));  // open: cin, cout
  Shift_Left_Two shift_left_two_1 (.Input(sign_extend_1_out), .out_2(shift_left_two_1_out_2));
  Multiplexer #(.width(32)) multiplexer_3 (
    .in0(adder_1_out), .in1(adder_2_out), .out(multiplexer_3_out), .sel(and_1_out));  // open: en
  and and_1 (and_1_out, control_unit_1_branch, xnor_1_out);
  xnor xnor_1 (xnor_1_out, control_unit_1_invzero, n32_bit_alu_1_zero);
  Multiplexer #(.width(32)) multiplexer_4 (
    .in0(multiplexer_3_out), .in1({adder_1_out[31:28], shift_left_2_jump_1_out}), .out(multiplexer_4_out),
    .sel(control_unit_1_jump));  // open: en
endmodule

// FLD
module Fields (
  input  [31:0] in,
  output [5:0] O,
  output [4:0] S,
  output [4:0] T,
  output [4:0] D,
  output [4:0] A,
  output [5:0] F,
  output [15:0] I_IMM,
  output [25:0] J_IMM
);


  assign A = in[25:21];
  assign D = in[20:16];
  assign F = in[31:26];
  assign I_IMM = in[31:16];
  assign J_IMM = in[31:6];
  assign O = in[5:0];
  assign S = in[10:6];
  assign T = in[15:11];
endmodule

module Shift_Left_2_Jump (
  input  [25:0] in,
  output [27:0] out
);


  assign out = {in, 2'b00};
endmodule

module ALUOPGen (
  input  Opp3,
  input  Opp2,
  input  Opp1,
  input  Opp0,
  input  funct5,
  input  funct3,
  input  funct2,
  input  funct1,
  input  funct0,
  output ALUOP3,
  output ALUOP2,
  output ALUOP1,
  output ALUOP0
);

  wire and_1_out, and_2_out, and_3_out, and_4_out, and_5_out, and_6_out, and_7_out, and_8_out, and_9_out,
       and_10_out, not_1_out, not_2_out, not_3_out, not_4_out, not_5_out, not_6_out, not_7_out, not_8_out,
       not_9_out, not_10_out, not_11_out, not_12_out, not_13_out;

  not not_1 (not_1_out, Opp3);
  not not_2 (not_2_out, Opp2);
  not not_3 (not_3_out, Opp3);
  not not_4 (not_4_out, Opp3);
  not not_5 (not_5_out, Opp3);
  not not_6 (not_6_out, funct2);
  not not_7 (not_7_out, Opp3);
  not not_8 (not_8_out, Opp2);
  not not_9 (not_9_out, Opp3);
  not not_10 (not_10_out, Opp2);
  not not_11 (not_11_out, funct1);
  not not_12 (not_12_out, Opp3);
  not not_13 (not_13_out, Opp2);
  and and_1 (and_1_out, not_1_out, not_2_out, funct2, funct1);
  and and_2 (and_2_out, Opp1, funct5, funct3, funct2, funct1, funct0);
  and and_3 (and_3_out, not_3_out, funct1);
  and and_4 (and_4_out, not_4_out, Opp2);
  and and_5 (and_5_out, not_5_out, not_6_out);
  and and_6 (and_6_out, not_7_out, Opp2);
  and and_7 (and_7_out, Opp3, not_8_out);
  and and_8 (and_8_out, not_9_out, not_10_out, not_11_out, funct0);
  and and_9 (and_9_out, not_12_out, not_13_out, funct3);
  and and_10 (and_10_out, Opp3, Opp0);
  or or_1 (ALUOP3, and_1_out, and_2_out);
  or or_2 (ALUOP2, and_3_out, Opp1, and_4_out);
  or or_3 (ALUOP1, and_5_out, and_6_out, and_7_out);
  or or_4 (ALUOP0, and_8_out, and_9_out, Opp1, and_10_out);
endmodule
