// Logisim project calculatorCPU.circ as structural Verilog
module main (
);

  wire _0_out, _1_out, _2_out, _3_out, _4_out, _5_out, _6_out, _7_out, _8_out, _9_out, button_2_out,
       button_3_out, button_4_out, button_5_out, button_out, C_out, keypad_controller_1_write;
  wire [2:0] lcd_controller_1__7_segment_3_2, lcd_controller_1__7_segment_4_2,
       lcd_controller_1__7_segment_5_2, lcd_controller_1__7_segment_6_2, lcd_controller_1__7_segment_7_2,
       lcd_controller_1__7_segment_8_2, lcd_controller_1__7_segment_9_2, lcd_controller_1_minus_2;
  wire [3:0] lcd_controller_1__7_segment_3, lcd_controller_1__7_segment_4, lcd_controller_1__7_segment_5,
       lcd_controller_1__7_segment_6, lcd_controller_1__7_segment_7, lcd_controller_1__7_segment_8,
       lcd_controller_1__7_segment_9, lcd_controller_1_minus;
  wire [6:0] lcd_controller_1__7_segment_0, lcd_controller_1__7_segment_1, lcd_controller_1__7_segment_2;
  wire [31:0] keypad_controller_1_output, undriven, undriven_2;

  _7_Segment_Display u_7_segment_display_1 (
    .g(lcd_controller_1_minus[0]), .f(lcd_controller_1_minus[1]), .a(lcd_controller_1_minus[2]),
    .b(lcd_controller_1_minus[3]), .e(lcd_controller_1_minus_2[0]), .d(lcd_controller_1_minus_2[1]),
    .c(lcd_controller_1_minus_2[2]));  // open: dp
  _7_Segment_Display u_7_segment_display_2 (
    .g(lcd_controller_1__7_segment_9[0]), .f(lcd_controller_1__7_segment_9[1]),
    .a(lcd_controller_1__7_segment_9[2]), .b(lcd_controller_1__7_segment_9[3]),
    .e(lcd_controller_1__7_segment_9_2[0]), .d(lcd_controller_1__7_segment_9_2[1]),
    .c(lcd_controller_1__7_segment_9_2[2]));  // open: dp
  LCD_Controller lcd_controller_1 (
    .From__t8(undriven), .Minus({lcd_controller_1_minus_2, lcd_controller_1_minus}),
    ._7_Segment_9({lcd_controller_1__7_segment_9_2, lcd_controller_1__7_segment_9}),
    ._7_Segment_8({lcd_controller_1__7_segment_8_2, lcd_controller_1__7_segment_8}),
    ._7_Segment_7({lcd_controller_1__7_segment_7_2, lcd_controller_1__7_segment_7}),
    ._7_Segment_6({lcd_controller_1__7_segment_6_2, lcd_controller_1__7_segment_6}),
    ._7_Segment_5({lcd_controller_1__7_segment_5_2, lcd_controller_1__7_segment_5}),
    ._7_Segment_4({lcd_controller_1__7_segment_4_2, lcd_controller_1__7_segment_4}),
    ._7_Segment_3({lcd_controller_1__7_segment_3_2, lcd_controller_1__7_segment_3}),
    ._7_Segment_2(lcd_controller_1__7_segment_2), ._7_Segment_1(lcd_controller_1__7_segment_1),
    ._7_Segment_0(lcd_controller_1__7_segment_0));
  Keypad_Controller keypad_controller_1 (
    .C(C_out), .in_2(button_out), .in_3(button_5_out), .in_4(button_4_out), .in_5(button_3_out),
    .in_6(button_2_out), ._9(_9_out), ._8(_8_out), ._7(_7_out), ._6(_6_out), ._5(_5_out), ._4(_4_out),
    ._3(_3_out), ._2(_2_out), ._1(_1_out), ._0(_0_out), .From__t9(undriven_2),
    .Write(keypad_controller_1_write), .Output(keypad_controller_1_output));
  _7_Segment_Display u_7_segment_display_3 (
    .g(lcd_controller_1__7_segment_8[0]), .f(lcd_controller_1__7_segment_8[1]),
    .a(lcd_controller_1__7_segment_8[2]), .b(lcd_controller_1__7_segment_8[3]),
    .e(lcd_controller_1__7_segment_8_2[0]), .d(lcd_controller_1__7_segment_8_2[1]),
    .c(lcd_controller_1__7_segment_8_2[2]));  // open: dp
  _7_Segment_Display u_7_segment_display_4 (
    .g(lcd_controller_1__7_segment_7[0]), .f(lcd_controller_1__7_segment_7[1]),
    .a(lcd_controller_1__7_segment_7[2]), .b(lcd_controller_1__7_segment_7[3]),
    .e(lcd_controller_1__7_segment_7_2[0]), .d(lcd_controller_1__7_segment_7_2[1]),
    .c(lcd_controller_1__7_segment_7_2[2]));  // open: dp
  _7_Segment_Display u_7_segment_display_5 (
    .g(lcd_controller_1__7_segment_6[0]), .f(lcd_controller_1__7_segment_6[1]),
    .a(lcd_controller_1__7_segment_6[2]), .b(lcd_controller_1__7_segment_6[3]),
    .e(lcd_controller_1__7_segment_6_2[0]), .d(lcd_controller_1__7_segment_6_2[1]),
    .c(lcd_controller_1__7_segment_6_2[2]));  // open: dp
  _7_Segment_Display u_7_segment_display_6 (
    .g(lcd_controller_1__7_segment_5[0]), .f(lcd_controller_1__7_segment_5[1]),
    .a(lcd_controller_1__7_segment_5[2]), .b(lcd_controller_1__7_segment_5[3]),
    .e(lcd_controller_1__7_segment_5_2[0]), .d(lcd_controller_1__7_segment_5_2[1]),
    .c(lcd_controller_1__7_segment_5_2[2]));  // open: dp
  Button _7 (.out(_7_out));
  Button _4 (.out(_4_out));
  Button _1 (.out(_1_out));
  Button _0 (.out(_0_out));
  _7_Segment_Display u_7_segment_display_7 (
    .g(lcd_controller_1__7_segment_4[0]), .f(lcd_controller_1__7_segment_4[1]),
    .a(lcd_controller_1__7_segment_4[2]), .b(lcd_controller_1__7_segment_4[3]),
    .e(lcd_controller_1__7_segment_4_2[0]), .d(lcd_controller_1__7_segment_4_2[1]),
    .c(lcd_controller_1__7_segment_4_2[2]));  // open: dp
  _7_Segment_Display u_7_segment_display_8 (
    .g(lcd_controller_1__7_segment_3[0]), .f(lcd_controller_1__7_segment_3[1]),
    .a(lcd_controller_1__7_segment_3[2]), .b(lcd_controller_1__7_segment_3[3]),
    .e(lcd_controller_1__7_segment_3_2[0]), .d(lcd_controller_1__7_segment_3_2[1]),
    .c(lcd_controller_1__7_segment_3_2[2]));  // open: dp
  Button _8 (.out(_8_out));
  Button _5 (.out(_5_out));
  Button _2 (.out(_2_out));
  Button C (.out(C_out));
  _7_Segment_Display u_7_segment_display_9 (
    .g(lcd_controller_1__7_segment_1[0]), .f(lcd_controller_1__7_segment_1[1]),
    .a(lcd_controller_1__7_segment_1[2]), .b(lcd_controller_1__7_segment_1[3]),
    .e(lcd_controller_1__7_segment_1[4]), .d(lcd_controller_1__7_segment_1[5]),
    .c(lcd_controller_1__7_segment_1[6]));  // open: dp
  _7_Segment_Display u_7_segment_display_10 (
    .g(lcd_controller_1__7_segment_2[0]), .f(lcd_controller_1__7_segment_2[1]),
    .a(lcd_controller_1__7_segment_2[2]), .b(lcd_controller_1__7_segment_2[3]),
    .e(lcd_controller_1__7_segment_2[4]), .d(lcd_controller_1__7_segment_2[5]),
    .c(lcd_controller_1__7_segment_2[6]));  // open: dp
  Button _9 (.out(_9_out));
  Button _6 (.out(_6_out));
  Button _3 (.out(_3_out));
  Button button (.out(button_out));
  _7_Segment_Display u_7_segment_display_11 (
    .g(lcd_controller_1__7_segment_0[0]), .f(lcd_controller_1__7_segment_0[1]),
    .a(lcd_controller_1__7_segment_0[2]), .b(lcd_controller_1__7_segment_0[3]),
    .e(lcd_controller_1__7_segment_0[4]), .d(lcd_controller_1__7_segment_0[5]),
    .c(lcd_controller_1__7_segment_0[6]));  // open: dp
  Button button_2 (.out(button_2_out));
  Button button_3 (.out(button_3_out));
  Button button_4 (.out(button_4_out));
  Button button_5 (.out(button_5_out));

  // Notes on the sheet:
  //   From $t8
  //   From $t9
  //   Write Data to $t9
  //   Write Signal for $t9
endmodule

module LCD_Controller (
  input  [31:0] From__t8,
  output [6:0] Minus,
  output [6:0] _7_Segment_9,
  output [6:0] _7_Segment_8,
  output [6:0] _7_Segment_7,
  output [6:0] _7_Segment_6,
  output [6:0] _7_Segment_5,
  output [6:0] _7_Segment_4,
  output [6:0] _7_Segment_3,
  output [6:0] _7_Segment_2,
  output [6:0] _7_Segment_1,
  output [6:0] _7_Segment_0
);

  wire [3:0] binarytobcd_1_bcd0, binarytobcd_1_bcd1, binarytobcd_1_bcd2, binarytobcd_1_bcd3,
       binarytobcd_1_bcd4, binarytobcd_1_bcd5, binarytobcd_1_bcd6, binarytobcd_1_bcd7, binarytobcd_1_bcd8,
       binarytobcd_1_bcd9;

  BinaryToBCD binarytobcd_1 (
    .Input(From__t8), .Minus(Minus[0]), .BCD9(binarytobcd_1_bcd9), .BCD8(binarytobcd_1_bcd8),
    .BCD7(binarytobcd_1_bcd7), .BCD6(binarytobcd_1_bcd6), .BCD5(binarytobcd_1_bcd5),
    .BCD4(binarytobcd_1_bcd4), .BCD3(binarytobcd_1_bcd3), .BCD2(binarytobcd_1_bcd2),
    .BCD1(binarytobcd_1_bcd1), .BCD0(binarytobcd_1_bcd0));
  _7_Segment_Controller u_7_segment_controller_1 (.BCD(binarytobcd_1_bcd9), .out_2(_7_Segment_9));
  _7_Segment_Controller u_7_segment_controller_2 (.BCD(binarytobcd_1_bcd8), .out_2(_7_Segment_8));
  _7_Segment_Controller u_7_segment_controller_3 (.BCD(binarytobcd_1_bcd7), .out_2(_7_Segment_7));
  _7_Segment_Controller u_7_segment_controller_4 (.BCD(binarytobcd_1_bcd6), .out_2(_7_Segment_6));
  _7_Segment_Controller u_7_segment_controller_5 (.BCD(binarytobcd_1_bcd5), .out_2(_7_Segment_5));
  _7_Segment_Controller u_7_segment_controller_6 (.BCD(binarytobcd_1_bcd4), .out_2(_7_Segment_4));
  _7_Segment_Controller u_7_segment_controller_7 (.BCD(binarytobcd_1_bcd3), .out_2(_7_Segment_3));
  _7_Segment_Controller u_7_segment_controller_8 (.BCD(binarytobcd_1_bcd2), .out_2(_7_Segment_2));
  _7_Segment_Controller u_7_segment_controller_9 (.BCD(binarytobcd_1_bcd1), .out_2(_7_Segment_1));
  _7_Segment_Controller u_7_segment_controller_10 (.BCD(binarytobcd_1_bcd0), .out_2(_7_Segment_0));

  assign Minus[6:1] = {6{1'b0}};
endmodule

module _7_Segment_Controller (
  input  [3:0] BCD,
  output [6:0] out_2
);

  wire and_1_out, and_2_out, and_3_out, and_4_out, and_5_out, and_6_out, and_7_out, and_8_out, and_9_out,
       and_10_out, and_11_out, and_12_out, and_13_out, and_14_out, and_15_out, and_16_out, not_1_out,
       not_2_out, not_3_out, not_4_out, not_5_out, not_6_out, not_7_out, not_8_out, not_9_out, not_10_out,
       not_11_out, not_12_out, not_13_out, not_14_out, not_15_out, not_16_out, not_17_out, not_18_out,
       not_19_out, not_20_out, not_21_out;

  not not_1 (not_1_out, BCD[2]);
  not not_2 (not_2_out, BCD[0]);
  not not_3 (not_3_out, BCD[1]);
  not not_4 (not_4_out, BCD[1]);
  not not_5 (not_5_out, BCD[0]);
  not not_6 (not_6_out, BCD[1]);
  not not_7 (not_7_out, BCD[0]);
  not not_8 (not_8_out, BCD[2]);
  not not_9 (not_9_out, BCD[0]);
  not not_10 (not_10_out, BCD[1]);
  not not_11 (not_11_out, BCD[0]);
  not not_12 (not_12_out, BCD[2]);
  not not_13 (not_13_out, BCD[0]);
  not not_14 (not_14_out, BCD[0]);
  not not_15 (not_15_out, BCD[2]);
  not not_16 (not_16_out, BCD[0]);
  not not_17 (not_17_out, BCD[2]);
  not not_18 (not_18_out, BCD[0]);
  not not_19 (not_19_out, BCD[1]);
  not not_20 (not_20_out, BCD[1]);
  and and_1 (and_1_out, not_1_out, BCD[1]);
  and and_2 (and_2_out, BCD[1], not_2_out);
  and and_3 (and_3_out, BCD[2], not_3_out);
  and and_4 (and_4_out, not_4_out, not_5_out);
  and and_5 (and_5_out, BCD[2], not_6_out);
  and and_6 (and_6_out, BCD[2], not_7_out);
  and and_7 (and_7_out, not_8_out, not_9_out);
  and and_8 (and_8_out, BCD[2], BCD[0]);
  not not_21 (not_21_out, BCD[2]);
  and and_9 (and_9_out, not_10_out, not_11_out);
  and and_10 (and_10_out, BCD[1], BCD[0]);
  and and_11 (and_11_out, not_12_out, not_13_out);
  and and_12 (and_12_out, BCD[1], not_14_out);
  and and_13 (and_13_out, not_15_out, not_16_out);
  and and_14 (and_14_out, not_17_out, BCD[1]);
  and and_15 (and_15_out, BCD[1], not_18_out);
  and and_16 (and_16_out, BCD[2], not_19_out, BCD[0]);
  or or_1 (out_2[6], not_20_out, BCD[0], BCD[2]);
  or or_2 (out_2[0], and_1_out, and_2_out, and_3_out, BCD[3]);
  or or_3 (out_2[1], and_4_out, and_5_out, and_6_out, BCD[3]);
  or or_4 (out_2[2], and_7_out, BCD[1], and_8_out, BCD[3]);
  or or_5 (out_2[3], not_21_out, and_9_out, and_10_out);
  or or_6 (out_2[4], and_11_out, and_12_out);
  or or_7 (out_2[5], and_13_out, and_14_out, and_15_out, and_16_out);
endmodule

module BinaryToBCD (
  input  [31:0] Input,
  output Minus,
  output [3:0] BCD9,
  output [3:0] BCD8,
  output [3:0] BCD7,
  output [3:0] BCD6,
  output [3:0] BCD5,
  output [3:0] BCD4,
  output [3:0] BCD3,
  output [3:0] BCD2,
  output [3:0] BCD1,
  output [3:0] BCD0
);

  wire [27:0] subtractor_1_out, subtractor_2_out, subtractor_3_out, subtractor_4_out, subtractor_5_out,
       subtractor_6_out, subtractor_7_out, subtractor_8_out, subtractor_9_out;
  wire [31:0] adder_1_out, divider_1_out, divider_2_out, divider_3_out, divider_4_out, divider_5_out,
       divider_6_out, divider_7_out, divider_8_out, multiplexer_1_out, multiplier_1_out, multiplier_2_out,
       multiplier_3_out, multiplier_4_out, multiplier_5_out, multiplier_6_out, multiplier_7_out,
       multiplier_8_out, multiplier_9_out, not_1_out;
  wire [31:4] divider_9_out;

  assign not_1_out = ~Input;  // NOT_Gate not_1, 32 bits wide
  Adder #(.width(32)) adder_1 (.a(not_1_out), .b(32'h1), .out(adder_1_out));  // open: cin, cout
  Multiplexer #(.width(32)) multiplexer_1 (
    .in0(Input), .in1(adder_1_out), .out(multiplexer_1_out), .sel(Input[31]));  // open: en
  Subtractor #(.width(32)) subtractor_1 (
    .a(multiplexer_1_out), .b(multiplier_1_out), .out({subtractor_1_out, BCD0}));  // open: bin, bout
  Multiplier #(.width(32)) multiplier_1 (.a(divider_1_out), .b(32'ha), .out(multiplier_1_out));  // open: cin, cout
  Divider #(.width(32)) divider_1 (.a(multiplexer_1_out), .b(32'ha), .out(divider_1_out));  // open: upper, rem
  Subtractor #(.width(32)) subtractor_2 (
    .a(divider_1_out), .b(multiplier_2_out), .out({subtractor_2_out, BCD1}));  // open: bin, bout
  Multiplier #(.width(32)) multiplier_2 (.a(divider_2_out), .b(32'ha), .out(multiplier_2_out));  // open: cin, cout
  Divider #(.width(32)) divider_2 (.a(divider_1_out), .b(32'ha), .out(divider_2_out));  // open: upper, rem
  Subtractor #(.width(32)) subtractor_3 (
    .a(divider_2_out), .b(multiplier_3_out), .out({subtractor_3_out, BCD2}));  // open: bin, bout
  Multiplier #(.width(32)) multiplier_3 (.a(divider_3_out), .b(32'ha), .out(multiplier_3_out));  // open: cin, cout
  Divider #(.width(32)) divider_3 (.a(divider_2_out), .b(32'ha), .out(divider_3_out));  // open: upper, rem
  Subtractor #(.width(32)) subtractor_4 (
    .a(divider_3_out), .b(multiplier_4_out), .out({subtractor_4_out, BCD3}));  // open: bin, bout
  Multiplier #(.width(32)) multiplier_4 (.a(divider_4_out), .b(32'ha), .out(multiplier_4_out));  // open: cin, cout
  Divider #(.width(32)) divider_4 (.a(divider_3_out), .b(32'ha), .out(divider_4_out));  // open: upper, rem
  Subtractor #(.width(32)) subtractor_5 (
    .a(divider_4_out), .b(multiplier_5_out), .out({subtractor_5_out, BCD4}));  // open: bin, bout
  Multiplier #(.width(32)) multiplier_5 (.a(divider_5_out), .b(32'ha), .out(multiplier_5_out));  // open: cin, cout
  Divider #(.width(32)) divider_5 (.a(divider_4_out), .b(32'ha), .out(divider_5_out));  // open: upper, rem
  Subtractor #(.width(32)) subtractor_6 (
    .a(divider_5_out), .b(multiplier_6_out), .out({subtractor_6_out, BCD5}));  // open: bin, bout
  Multiplier #(.width(32)) multiplier_6 (.a(divider_6_out), .b(32'ha), .out(multiplier_6_out));  // open: cin, cout
  Divider #(.width(32)) divider_6 (.a(divider_5_out), .b(32'ha), .out(divider_6_out));  // open: upper, rem
  Subtractor #(.width(32)) subtractor_7 (
    .a(divider_6_out), .b(multiplier_7_out), .out({subtractor_7_out, BCD6}));  // open: bin, bout
  Multiplier #(.width(32)) multiplier_7 (.a(divider_7_out), .b(32'ha), .out(multiplier_7_out));  // open: cin, cout
  Divider #(.width(32)) divider_7 (.a(divider_6_out), .b(32'ha), .out(divider_7_out));  // open: upper, rem
  Subtractor #(.width(32)) subtractor_8 (
    .a(divider_7_out), .b(multiplier_8_out), .out({subtractor_8_out, BCD7}));  // open: bin, bout
  Multiplier #(.width(32)) multiplier_8 (.a(divider_8_out), .b(32'ha), .out(multiplier_8_out));  // open: cin, cout
  Divider #(.width(32)) divider_8 (.a(divider_7_out), .b(32'ha), .out(divider_8_out));  // open: upper, rem
  Subtractor #(.width(32)) subtractor_9 (
    .a(divider_8_out), .b(multiplier_9_out), .out({subtractor_9_out, BCD8}));  // open: bin, bout
  Multiplier #(.width(32)) multiplier_9 (
    .a({divider_9_out, BCD9}), .b(32'ha), .out(multiplier_9_out));  // open: cin, cout
  Divider #(.width(32)) divider_9 (.a(divider_8_out), .b(32'ha), .out({divider_9_out, BCD9}));  // open: upper, rem

  assign Minus = Input[31];
endmodule

module Keypad_Controller (
  input  C,
  input  in_2,
  input  in_3,
  input  in_4,
  input  in_5,
  input  in_6,
  input  _9,
  input  _8,
  input  _7,
  input  _6,
  input  _5,
  input  _4,
  input  _3,
  input  _2,
  input  _1,
  input  _0,
  input  [31:0] From__t9,
  output Write,
  output [31:0] Output
);

  wire iszero_1_out_2, iszero_2_out_2, not_1_out;
  wire [3:0] or_4_out;
  wire [15:0] controlled_buffer_1_out;

  assign controlled_buffer_1_out[0] = iszero_1_out_2 ? C : 1'bz;  // Controlled_Buffer controlled_buffer_1
  assign controlled_buffer_1_out[1] = iszero_1_out_2 ? in_2 : 1'bz;  // Controlled_Buffer controlled_buffer_2
  assign controlled_buffer_1_out[2] = iszero_1_out_2 ? in_3 : 1'bz;  // Controlled_Buffer controlled_buffer_3
  assign controlled_buffer_1_out[3] = iszero_1_out_2 ? in_4 : 1'bz;  // Controlled_Buffer controlled_buffer_4
  assign controlled_buffer_1_out[4] = iszero_1_out_2 ? in_5 : 1'bz;  // Controlled_Buffer controlled_buffer_5
  assign controlled_buffer_1_out[5] = iszero_1_out_2 ? in_6 : 1'bz;  // Controlled_Buffer controlled_buffer_6
  assign controlled_buffer_1_out[6] = iszero_1_out_2 ? _9 : 1'bz;  // Controlled_Buffer controlled_buffer_7
  assign controlled_buffer_1_out[7] = iszero_1_out_2 ? _8 : 1'bz;  // Controlled_Buffer controlled_buffer_8
  assign controlled_buffer_1_out[8] = iszero_1_out_2 ? _7 : 1'bz;  // Controlled_Buffer controlled_buffer_9
  assign controlled_buffer_1_out[9] = iszero_1_out_2 ? _6 : 1'bz;  // Controlled_Buffer controlled_buffer_10
  assign controlled_buffer_1_out[10] = iszero_1_out_2 ? _5 : 1'bz;  // Controlled_Buffer controlled_buffer_11
  assign controlled_buffer_1_out[11] = iszero_1_out_2 ? _4 : 1'bz;  // Controlled_Buffer controlled_buffer_12
  assign controlled_buffer_1_out[12] = iszero_1_out_2 ? _3 : 1'bz;  // Controlled_Buffer controlled_buffer_13
  assign controlled_buffer_1_out[13] = iszero_1_out_2 ? _2 : 1'bz;  // Controlled_Buffer controlled_buffer_14
  assign controlled_buffer_1_out[14] = iszero_1_out_2 ? _1 : 1'bz;  // Controlled_Buffer controlled_buffer_15
  assign controlled_buffer_1_out[15] = iszero_1_out_2 ? _0 : 1'bz;  // Controlled_Buffer controlled_buffer_16
  isZero iszero_1 (.Input(From__t9), .out_2(iszero_1_out_2));
  or or_1 (or_4_out[3], controlled_buffer_1_out[0], controlled_buffer_1_out[1], controlled_buffer_1_out[2], controlled_buffer_1_out[3], controlled_buffer_1_out[4], controlled_buffer_1_out[5], controlled_buffer_1_out[6], controlled_buffer_1_out[7]);
  or or_2 (or_4_out[2], controlled_buffer_1_out[8], controlled_buffer_1_out[9], controlled_buffer_1_out[10], controlled_buffer_1_out[11], controlled_buffer_1_out[0], controlled_buffer_1_out[1], controlled_buffer_1_out[2], controlled_buffer_1_out[3]);
  or or_3 (or_4_out[1], controlled_buffer_1_out[12], controlled_buffer_1_out[13], controlled_buffer_1_out[9], controlled_buffer_1_out[8], controlled_buffer_1_out[5], controlled_buffer_1_out[4], controlled_buffer_1_out[1], controlled_buffer_1_out[0]);
  or or_4 (or_4_out[0], controlled_buffer_1_out[12], controlled_buffer_1_out[14], controlled_buffer_1_out[10], controlled_buffer_1_out[8], controlled_buffer_1_out[6], controlled_buffer_1_out[4], controlled_buffer_1_out[2], controlled_buffer_1_out[0]);
  isZero iszero_2 (.Input({{16{1'b0}}, controlled_buffer_1_out}), .out_2(iszero_2_out_2));
  not not_1 (not_1_out, iszero_2_out_2);
  assign Write = not_1_out ? 1'b1 : 1'bz;  // Controlled_Buffer controlled_buffer_17
  assign Output = not_1_out ? {28'h8000000, or_4_out} : 32'bz;  // Controlled_Buffer controlled_buffer_18
endmodule

module isZero (
  input  [31:0] Input,
  output out_2
);

  wire or_1_out;

  not not_1 (out_2, or_1_out);
  or or_1 (or_1_out, Input[0], Input[1], Input[2], Input[3], Input[4], Input[5], Input[6], Input[7], Input[8], Input[9], Input[10], Input[11], Input[12], Input[13], Input[14], Input[15], Input[16], Input[17], Input[18], Input[19], Input[20], Input[21], Input[22], Input[23], Input[24], Input[25], Input[26], Input[27], Input[28], Input[29], Input[30], Input[31]);
endmodule
